# Fritzing sketch echo-gun (saved by Fritzing 0.9.3b)

parts:
  Part1 = Arduino Uno (Rev3)
  hc-sr1 = hc-sr04
  SP1 = SPEAKER [package=pcb_mount_speaker]
  Part2 = LED Matrix - Serial Interface - Red/Green/Blue
  S1 = Pushbutton [package="[THT]"]
  R1 = Resistor [tolerance=±5% resistance=220 package=THT]

nets:
  N1: Part1.D12/MISO, hc-sr1.Echo
  N2: Part1.D13/SCK, hc-sr1.Trig
  GND: Part1.GND, hc-sr1.GND, SP1.+, Part2.SCK, R1.Pin_1
  N3: Part1.D2, S1.Pin_1, S1.Pin_2, R1.Pin_0
  N4: Part1.D3_PWM, SP1.-
  N5: Part1.D5_PWM, Part2.MISO
  N6: Part1.D6_PWM, Part2.GND
  N7: Part1.D7, Part2.CS
  5V: Part1.5V, Part2.VCC, S1.Pin_3, S1.Pin_4
