# Fritzing sketch first-robot (saved by Fritzing 0.9.3b)
breadboards: 1

parts:
  Part1 = Arduino Uno (Rev3)
  hc-sr1 = hc-sr04
  U2 = L298 [package=multiwatt15_6400bgheatsink]
  M1 = DC Motor  # not connected
  M2 = DC Motor  # not connected
  M4 = Dagu DGServo 9g (Top view) [part_number=RS001B]
  VCC1 = Battery  # not connected
  VCC2 = Battery block 9V  # not connected

nets:
  N1: Part1.D9_PWM, U2.OUT2
  N2: Part1.D10_PWM/SS, U2.ENA
  N3: Part1.D12/MISO, hc-sr1.Trig
  N4: Part1.D13/SCK, hc-sr1.Echo
  N5: Part1.D2, U2.CSA
  N6: Part1.D3_PWM, U2.OUT1
  N7: Part1.D4, U2.VS
  N8: Part1.D5_PWM, U2.IN1
  N9: Part1.D6_PWM, M4.pulse
  5V: Part1.5V, hc-sr1.VCC
  GND: Part1.GND, hc-sr1.GND
