# Fritzing sketch r2d2-ir-remote (saved by Fritzing 0.9.3b)
breadboards: 1

parts:
  Part1 = Arduino Uno (Rev3)
  U2 = L298 [package=multiwatt15_6400bgheatsink]
  M1 = DC Motor  # not connected
  M2 = DC Motor  # not connected
  VCC1 = Battery
  VCC2 = Battery block 9V  # not connected
  M3 = Stepper Motor - Bipolar  # not connected
  Pololu_A1 = Pololu A4988 [package=SO16]
  IR1 = TSOP312.., 314.. [package=THT]

nets:
  N1: Part1.D8, Pololu_A1.SLEEP
  N2: Part1.D9_PWM, Pololu_A1.RESET
  N3: Part1.D10_PWM/SS, Pololu_A1.MS3
  N4: Part1.D11_PWM/MOSI, Pololu_A1.MS2
  N5: Part1.D13/SCK, IR1.GND
  N6: Part1.D2, U2.CSA
  N7: Part1.D3_PWM, U2.OUT1
  N8: Part1.D4, U2.VS
  N9: Part1.D5_PWM, U2.IN1
  N10: U2.IN2, VCC1.+, Pololu_A1.ENABLE, IR1.Vs
  N11: U2.GND, VCC1.-, Pololu_A1.DIR, IR1.Data
